// Logisim project Ejercicio2.circ as structural Verilog: 3 circuits, main circuit main
module main (
  input  [2:0] ABC,
  input  [2:0] DEF,
  input  [2:0] GHI
);

  wire Procesar_out;

  Button Procesar (.out(Procesar_out));
endmodule

module Memoria_Interna (
  input  [2:0] EntradaDatos,
  input  in_2,
  input  [2:0] Address
);

  wire d_ff_1_q, d_ff_2_q, d_ff_3_q, d_ff_4_q, d_ff_5_q, d_ff_6_q, d_ff_7_q, d_ff_8_q, d_ff_9_q, d_ff_10_q,
       d_ff_11_q, d_ff_12_q, d_ff_13_q, d_ff_14_q, d_ff_15_q, d_ff_16_q, d_ff_17_q, d_ff_18_q, d_ff_19_q,
       d_ff_20_q, d_ff_21_q, d_ff_22_q, d_ff_23_q, d_ff_24_q, decoder_1_out0, decoder_1_out1, decoder_1_out2,
       decoder_1_out3, decoder_1_out4, decoder_1_out5, decoder_1_out6, decoder_1_out7, undriven, undriven_2,
       undriven_3, undriven_4, undriven_5, undriven_6, undriven_7, undriven_8, undriven_9, undriven_10,
       undriven_11, undriven_12, undriven_13, undriven_14, undriven_15, undriven_16;

  Decoder #(.select(3)) decoder_1 (
    .out0(decoder_1_out0), .out1(decoder_1_out1), .out2(decoder_1_out2), .out3(decoder_1_out3),
    .out4(decoder_1_out4), .out5(decoder_1_out5), .out6(decoder_1_out6), .out7(decoder_1_out7),
    .sel(Address), .en(in_2));
  D_Flip_Flop d_ff_1 (.D(EntradaDatos[0]), .clk(decoder_1_out0), .Q(d_ff_1_q), .reset(undriven));  // open: Qn, preset
  D_Flip_Flop d_ff_2 (
    .D(EntradaDatos[1]), .clk(decoder_1_out0), .Q(d_ff_2_q), .preset(undriven), .reset(undriven_2));  // open: Qn
  D_Flip_Flop d_ff_3 (.D(EntradaDatos[2]), .clk(decoder_1_out0), .Q(d_ff_3_q), .preset(undriven_2));  // open: Qn, reset
  LED led_1 (.in(d_ff_1_q));
  LED led_2 (.in(d_ff_2_q));
  LED led_3 (.in(d_ff_3_q));
  D_Flip_Flop d_ff_4 (.D(EntradaDatos[0]), .clk(decoder_1_out1), .Q(d_ff_4_q), .reset(undriven_3));  // open: Qn, preset
  LED led_4 (.in(d_ff_4_q));
  D_Flip_Flop d_ff_5 (
    .D(EntradaDatos[1]), .clk(decoder_1_out1), .Q(d_ff_5_q), .preset(undriven_3), .reset(undriven_4));  // open: Qn
  LED led_5 (.in(d_ff_5_q));
  D_Flip_Flop d_ff_6 (.D(EntradaDatos[2]), .clk(decoder_1_out1), .Q(d_ff_6_q), .preset(undriven_4));  // open: Qn, reset
  LED led_6 (.in(d_ff_6_q));
  D_Flip_Flop d_ff_7 (.D(EntradaDatos[0]), .clk(decoder_1_out2), .Q(d_ff_7_q), .reset(undriven_5));  // open: Qn, preset
  LED led_7 (.in(d_ff_7_q));
  D_Flip_Flop d_ff_8 (
    .D(EntradaDatos[1]), .clk(decoder_1_out2), .Q(d_ff_8_q), .preset(undriven_5), .reset(undriven_6));  // open: Qn
  LED led_8 (.in(d_ff_8_q));
  D_Flip_Flop d_ff_9 (.D(EntradaDatos[2]), .clk(decoder_1_out2), .Q(d_ff_9_q), .preset(undriven_6));  // open: Qn, reset
  LED led_9 (.in(d_ff_9_q));
  D_Flip_Flop d_ff_10 (
    .D(EntradaDatos[0]), .clk(decoder_1_out3), .Q(d_ff_10_q), .reset(undriven_7));  // open: Qn, preset
  D_Flip_Flop d_ff_11 (
    .D(EntradaDatos[1]), .clk(decoder_1_out3), .Q(d_ff_11_q), .preset(undriven_7), .reset(undriven_8));  // open: Qn
  D_Flip_Flop d_ff_12 (
    .D(EntradaDatos[2]), .clk(decoder_1_out3), .Q(d_ff_12_q), .preset(undriven_8));  // open: Qn, reset
  LED led_10 (.in(d_ff_10_q));
  LED led_11 (.in(d_ff_11_q));
  LED led_12 (.in(d_ff_12_q));
  D_Flip_Flop d_ff_13 (
    .D(EntradaDatos[0]), .clk(decoder_1_out4), .Q(d_ff_13_q), .reset(undriven_9));  // open: Qn, preset
  D_Flip_Flop d_ff_14 (
    .D(EntradaDatos[1]), .clk(decoder_1_out4), .Q(d_ff_14_q), .preset(undriven_9), .reset(undriven_10));  // open: Qn
  D_Flip_Flop d_ff_15 (
    .D(EntradaDatos[2]), .clk(decoder_1_out4), .Q(d_ff_15_q), .preset(undriven_10));  // open: Qn, reset
  LED led_13 (.in(d_ff_13_q));
  LED led_14 (.in(d_ff_14_q));
  LED led_15 (.in(d_ff_15_q));
  D_Flip_Flop d_ff_16 (
    .D(EntradaDatos[0]), .clk(decoder_1_out5), .Q(d_ff_16_q), .reset(undriven_11));  // open: Qn, preset
  D_Flip_Flop d_ff_17 (
    .D(EntradaDatos[1]), .clk(decoder_1_out5), .Q(d_ff_17_q), .preset(undriven_11), .reset(undriven_12));  // open: Qn
  D_Flip_Flop d_ff_18 (
    .D(EntradaDatos[2]), .clk(decoder_1_out5), .Q(d_ff_18_q), .preset(undriven_12));  // open: Qn, reset
  LED led_16 (.in(d_ff_16_q));
  LED led_17 (.in(d_ff_17_q));
  LED led_18 (.in(d_ff_18_q));
  D_Flip_Flop d_ff_19 (
    .D(EntradaDatos[0]), .clk(decoder_1_out6), .Q(d_ff_19_q), .reset(undriven_13));  // open: Qn, preset
  D_Flip_Flop d_ff_20 (
    .D(EntradaDatos[1]), .clk(decoder_1_out6), .Q(d_ff_20_q), .preset(undriven_13), .reset(undriven_14));  // open: Qn
  D_Flip_Flop d_ff_21 (
    .D(EntradaDatos[2]), .clk(decoder_1_out6), .Q(d_ff_21_q), .preset(undriven_14));  // open: Qn, reset
  LED led_19 (.in(d_ff_19_q));
  LED led_20 (.in(d_ff_20_q));
  LED led_21 (.in(d_ff_21_q));
  D_Flip_Flop d_ff_22 (
    .D(EntradaDatos[0]), .clk(decoder_1_out7), .Q(d_ff_22_q), .reset(undriven_15));  // open: Qn, preset
  D_Flip_Flop d_ff_23 (
    .D(EntradaDatos[1]), .clk(decoder_1_out7), .Q(d_ff_23_q), .preset(undriven_15), .reset(undriven_16));  // open: Qn
  D_Flip_Flop d_ff_24 (
    .D(EntradaDatos[2]), .clk(decoder_1_out7), .Q(d_ff_24_q), .preset(undriven_16));  // open: Qn, reset
  LED led_22 (.in(d_ff_22_q));
  LED led_23 (.in(d_ff_23_q));
  LED led_24 (.in(d_ff_24_q));
endmodule

module FlipFlop_TipoD (
  input  D,
  input  P,
  output out_3
);

  wire nand_1_out, nand_2_out, nand_4_out, not_1_out;

  not not_1 (not_1_out, D);
  nand nand_1 (nand_1_out, D, P);
  nand nand_2 (nand_2_out, not_1_out, P);
  nand nand_3 (out_3, nand_1_out, nand_4_out);
  nand nand_4 (nand_4_out, out_3, nand_2_out);
endmodule
